# Fritzing sketch offices (saved by Fritzing 0.9.2b)
breadboards: 1

parts:
  Componente1 = Arduino Uno (Rev3)
  R1 = Resistor [tolerance=±5% resistance=270 package="1206 [SMD]"]
  R2 = Resistor [tolerance=±5% resistance=270 package="1206 [SMD]"]
  R3 = Resistor [tolerance=±5% resistance=270 package="1206 [SMD]"]
  LED1 = RGB LED (com. cathode, rbg) [package="5 mm [THT]"]
  Q2 = TIP120 Hi-Current Darlington Transistor
  D1 = Schottky Diode [part_number=1N5817 package="Melf DO-213 AB [SMD]"]
  S1 = Momentary Switch [package=ksa_sealed_tac_switch]
  R4 = Resistor [tolerance=±0.5% resistance=220 package="1206 [SMD]"]

nets:
  N1: Componente1.D8, S1.4
  N2: Componente1.D2, Q2.BASE
  N3: Componente1.5V, R1.Pin_1, R2.Pin_1, R3.Pin_1, S1.3
  N4: Componente1.GND, Q2.EMITTER, R4.Pin_1
  N5: R1.Pin_0, LED1.red_anode
  N6: R2.Pin_0, LED1.green_anode
  N7: R3.Pin_0, LED1.blue_anode
  N8: LED1.common_cathode, D1.anode
  N9: Q2.COLLECTOR, D1.cathode
  N10: S1.1, R4.Pin_0

notes:
  Offices: Prototype 1
  only use one arduino per office. However each gate corresponds a one teacher in the office
  Beyond office time, the teacher can use a button to notify he is present in your office
