# Fritzing sketch services-1 (saved by Fritzing 0.9.2b)
breadboards: 1

parts:
  Componente1 = Arduino Uno (Rev3)
  R1 = Resistor [tolerance=±5% resistance=270 package="1206 [SMD]"]
  R2 = Resistor [tolerance=±5% resistance=270 package="1206 [SMD]"]
  R3 = Resistor [tolerance=±5% resistance=270 package="1206 [SMD]"]
  LED1 = RGB LED (com. cathode, rbg) [package="5 mm [THT]"]
  Q2 = TIP120 Hi-Current Darlington Transistor
  D1 = Schottky Diode [part_number=1N5817 package="Melf DO-213 AB [SMD]"]

nets:
  N1: Componente1.D4, Q2.BASE
  N2: Componente1.5V, R1.Pin_1, R2.Pin_1, R3.Pin_1
  N3: Componente1.GND, Q2.EMITTER
  N4: R1.Pin_0, LED1.red_anode
  N5: R2.Pin_0, LED1.green_anode
  N6: R3.Pin_0, LED1.blue_anode
  N7: LED1.common_cathode, D1.anode
  N8: Q2.COLLECTOR, D1.cathode

notes:
  Services: Prototype 1
  Arduino board control all services in institution DARQ and Colégio das Artes
  — The light is white
