# Fritzing sketch services-2 (saved by Fritzing 0.9.2b)
breadboards: 1

parts:
  Componente1 = Arduino Uno (Rev3)
  R1 = Resistor [tolerance=±5% resistance=270 package="1206 [SMD]"]
  R2 = Resistor [tolerance=±5% resistance=270 package="1206 [SMD]"]
  R3 = Resistor [tolerance=±5% resistance=270 package="1206 [SMD]"]
  LED1 = RGB LED (com. cathode, rbg) [package="5 mm [THT]"]
  Q2 = TIP120 Hi-Current Darlington Transistor
  D1 = Schottky Diode [part_number=1N5817 package="Melf DO-213 AB [SMD]"]

nets:
  N1: Componente1.D9_PWM, R1.Pin_1
  N2: Componente1.D10_PWM/SS, R3.Pin_1
  N3: Componente1.D11_PWM/MOSI, R2.Pin_1
  N4: Componente1.D4, Q2.BASE
  N5: Componente1.GND, Q2.EMITTER
  N6: R1.Pin_0, LED1.red_anode
  N7: R2.Pin_0, LED1.green_anode
  N8: R3.Pin_0, LED1.blue_anode
  N9: LED1.common_cathode, D1.anode
  N10: Q2.COLLECTOR, D1.cathode

notes:
  Services: Prototype 2
  For other instituition
  — The light icolor is a varirable
